# Fritzing sketch liedetector (saved by Fritzing 0.7.0b)
breadboards: 1

parts:
  Arduino1 = Arduino
  R1 = Rotary Potentiometer (Small) [maximum_resistance=100kΩ]
  J1 = Piezo Speaker
  LED1 = RGB LED (com. cathode, rbg) [package="5 mm [THT]"]
  R2 = Resistor [tolerance=±5% resistance=330 package=THT]
  R3 = Resistor [tolerance=±5% resistance=330 package=THT]
  R4 = Resistor [tolerance=±5% resistance=330 package=THT]
  R5 = Resistor [tolerance=±5% resistance=470k package=THT]

nets:
  N1: Arduino1.D11, R4.Pin_0
  N2: Arduino1.D10, R3.Pin_0
  N3: Arduino1.D9, R2.Pin_0
  N4: Arduino1.D7, J1.pin2
  N5: Arduino1.+5V, R1.leg1
  N6: Arduino1.GND, R1.leg2, J1.pin1, LED1.common_cathode, R5.Pin_0
  N7: Arduino1.A0, R5.Pin_1
  N8: Arduino1.A1, R1.wiper
  N9: LED1.red_anode, R2.Pin_1
  N10: LED1.blue_anode, R3.Pin_1
  N11: LED1.green_anode, R4.Pin_1

notes:
  finger here
